# Fritzing sketch Untitled Sketch_q1 (saved by Fritzing 0.9.3b)
circuit board: 8.46667cm x 5.64444cm
breadboards: 1

parts:
  R1 = Resistor [tolerance=±5% resistance=220 package=THT]
  R3 = Resistor [tolerance=±5% resistance=220 package=THT]
  R4 = Resistor [tolerance=±5% resistance=220 package=THT]
  LED1 = LEDs [package=led10mm]
  D5 = Rectifier Diode [package="Melf DO-213 AA [SMD]"]
  D6 = Rectifier Diode [package="Melf DO-213 AA [SMD]"]
  D7 = Rectifier Diode [package="Melf DO-213 AA [SMD]"]
  D8 = Rectifier Diode [package="Melf DO-213 AA [SMD]"]
  D9 = Zener Diode [part_number=1N4732A breakdown_voltage=3.6V package="300 mil [THT]"]
  C1 = Electrolytic Capacitor [capacitance=1000µF package="300 mil [THT, electrolytic]"]
  V1 = AC Power [voltage=5 frequency=60]
  R5 = Resistor [tolerance=±5% resistance=220 package=THT]
  C2 = Ceramic Capacitor [capacitance=100nF package="100 mil [THT, multilayer]"]
  Z1 = VARISTOR [package=0402-res]
  F1 = FUSE [package=fuse_5mm]

nets:
  N1: R1.Pin_0, V1.V-
  N2: R1.Pin_1, D5.cathode, D6.anode, Z1.1
  N3: R3.Pin_0, C2.0, Z1.2, F1.2
  N4: R3.Pin_1, D7.anode, D8.cathode, C2.1
  N5: R4.Pin_0, R5.Pin_1
  N6: R4.Pin_1, LED1.A
  N7: LED1.C, D5.anode, D8.anode, D9.anode, C1.-
  N8: D6.cathode, D7.cathode, C1.+, R5.Pin_0
  N9: V1.V+, F1.1
